# Fritzing sketch socrates_wiring (saved by Fritzing 0.9.10b)
breadboards: 1

parts:
  Battery = LIPO-1000mAh [package=lipo-1000]
  5V_Regulator = Voltage Regulator [package=78xxl]
  12V_Regulator = Voltage Regulator [package=78xxl]
  IR_Illuminator = LTE-302 [package=lte-302]
  IR_Switch = MOSFET-NCHANNEL [package=to-92]
  Mod1 = Raspberry Pi 4B
  PIR = LM35 Temperature Sensor [thermistor_type=NTC package="TO92 [THT]"]

nets:
  N1: Battery.+, 5V_Regulator.IN, 12V_Regulator.IN
  GND: Battery.-, 5V_Regulator.GND, 12V_Regulator.GND, IR_Switch.D, Mod1.GND, PIR.GND
  N2: 5V_Regulator.OUT, Mod1.5V, PIR.+Vs
  N3: 12V_Regulator.OUT, IR_Illuminator.A
  N4: IR_Illuminator.C, IR_Switch.S
  N5: IR_Switch.G, Mod1.GPIO23
  N6: Mod1.GPIO16, PIR.Vout
